# Fritzing sketch Meditation Clock Schematic (saved by Fritzing 0.9.1b)
breadboards: 1

parts:
  Part1 = Arduino Uno (Rev3)
  U1 = CAPSENSE_PAD [package=capsense_pad]
  Grove1 = Grove 3 Axis Digital Accelerometer 16g
  Part2 = HC-SR04 Ultrasonic Rangemeter
  U2 = 7-SEGMENT-4DIGIT [package=7-segment-4digit-5641]
  Q1 = TRANSISTOR_NPN [package=to-92-ammo]
  Q2 = TRANSISTOR_NPN [package=to-92-ammo]
  R1 = Resistor [tolerance=±5% resistance=470 package=THT]
  R2 = Resistor [tolerance=±5% resistance=470 package=THT]
  R3 = Resistor [tolerance=±5% resistance=470 package=THT]
  R4 = Resistor [tolerance=±5% resistance=470 package=THT]
  R5 = Resistor [tolerance=±5% resistance=470 package=THT]
  R6 = Resistor [tolerance=±5% resistance=470 package=THT]
  R7 = Resistor [tolerance=±5% resistance=470 package=THT]
  R8 = Resistor [tolerance=±5% resistance=470 package=THT]  # not connected
  R9 = Resistor [tolerance=±5% resistance=1M package=THT]
  J1 = Basic Servo
  R10 = Resistor [tolerance=±5% resistance=5.1k package=THT]
  R11 = Resistor [tolerance=±5% resistance=5.1k package=THT]

nets:
  N1: Part1.A0, R9.Pin_1
  N2: Part1.A1, U1.RECEIVE
  N3: Part1.A2, Part2.Echo
  N4: Part1.A3, Part2.Trig
  N5: Part1.A4/SDA, Grove1.SDA
  N6: Part1.A5/SCL, Grove1.SCL
  N7: Part1.D8, R6.Pin_1
  N8: Part1.D9_PWM, R11.Pin_0
  N9: Part1.D10_PWM/SS, R10.Pin_1
  N10: Part1.D12/MISO, J1.pulse
  GND: Part1.D13/SCK, Grove1.GND, Part2.GND, Q1.E, Q2.E, J1.gnd
  N11: Part1.D2, R7.Pin_0
  N12: Part1.D3_PWM, R3.Pin_0
  N13: Part1.D4, R4.Pin_1
  N14: Part1.D5_PWM, R2.Pin_1
  N15: Part1.D6_PWM, R1.Pin_1
  N16: Part1.D7, R5.Pin_0
  VCC: Part1.5V, Grove1.VCC, Part2.VCC, J1.vcc
  N17: U1.RES, R9.Pin_0
  N18: U2.DIG3, Q2.C
  N19: U2.DIG4, Q1.C
  N20: U2.A, R7.Pin_1
  N21: U2.B, R3.Pin_1
  N22: U2.C, R4.Pin_0
  N23: U2.D, R2.Pin_0
  N24: U2.E, R1.Pin_0
  N25: U2.F, R5.Pin_1
  N26: U2.G, R6.Pin_0
  N27: Q1.B, R11.Pin_1
  N28: Q2.B, R10.Pin_0

custom parts:
  7-SEGMENT-4DIGIT: if you need make parts, send me e-mail and write. Price 1 part=0.9 WMZ (http://www.wmtransfer.com/) ~ 0.9 Euro
